// Logisim project muxrisccore.circ as structural Verilog: 2 circuits, main circuit main
module main (
);

  wire and_1_out, and_2_out, and_3_out, and_4_out, and_5_out, bitselector_11_out, bitselector_12_out,
       clock_1_out, clock_2_out, clock_3_out, clock_4_out, clock_5_out, comparator_1_eq, comparator_3_eq,
       comparator_4_eq, comparator_5_eq, comparator_6_eq, comparator_7_eq, comparator_7_lt, comparator_8_eq,
       comparator_8_lt, counter_1_q, fpcomparator_1_p8, fpcomparator_1_p9, multiplexer_1_out,
       multiplexer_5_out, not_1_out, not_2_out, not_3_out, or_1_out, or_2_out, or_4_out, or_5_out,
       register_3_q;
  wire [1:0] bitselector_9_out;
  wire [3:0] bitselector_8_out;
  wire [5:0] bitselector_5_out, bitselector_6_out, bitselector_7_out, bitselector_10_out;
  wire [15:0] bitselector_1_out, bitselector_2_out, bitselector_3_out, bitselector_4_out, bitselector_13_out,
       bitselector_14_out, counter_2_q, multiplexer_3_out, multiplexer_4_out;
  wire [63:0] fpcomparator_1_p6, multiplexer_2_out, multiplexer_6_out, or_3_out, ram_1_dout, register_1_q,
       register_2_q, registry_1_regxout, shifter_1_out;

  BitSelector #(.group(16), .width(64)) bitselector_1 (.in(register_1_q), .out(bitselector_1_out), .sel(2'b11));
  BitSelector #(.group(16), .width(64)) bitselector_2 (.in(register_1_q), .out(bitselector_2_out), .sel(2'b10));
  BitSelector #(.group(16), .width(64)) bitselector_3 (.in(register_1_q), .out(bitselector_3_out), .sel(2'b01));
  BitSelector #(.group(16), .width(64)) bitselector_4 (.in(register_1_q), .out(bitselector_4_out), .sel(2'b00));
  Register #(.trigger("falling"), .width(64)) register_1 (
    .D(ram_1_dout), .en(or_1_out), .clk(clock_1_out), .Q(register_1_q));  // open: clr
  or or_1 (or_1_out, or_4_out, comparator_1_eq);
  Comparator #(.width(64)) comparator_1 (.a({64{1'b0}}), .b(register_1_q), .eq(comparator_1_eq));  // open: gt, lt
  Clock clock_1 (.out(clock_1_out));
  BitSelector #(.group(6), .width(16)) bitselector_5 (.in(bitselector_1_out), .out(bitselector_5_out), .sel(2'b00));
  BitSelector #(.group(6), .width(16)) bitselector_6 (.in(bitselector_2_out), .out(bitselector_6_out), .sel(2'b00));
  BitSelector #(.group(6), .width(16)) bitselector_7 (.in(bitselector_3_out), .out(bitselector_7_out), .sel(2'b00));
  BitSelector #(.group(4), .width(16)) bitselector_8 (.in(bitselector_4_out), .out(bitselector_8_out), .sel(2'b00));
  BitSelector #(.group(2), .width(16)) bitselector_9 (.in(bitselector_3_out), .out(bitselector_9_out), .sel(3'b100));
  BitSelector #(.group(6), .width(16)) bitselector_10 (.in(bitselector_3_out), .out(bitselector_10_out), .sel(2'b00));
  BitSelector #(.width(64)) bitselector_11 (.in(fpcomparator_1_p6), .out(bitselector_11_out), .sel(bitselector_7_out));
  Comparator #(.mode("unsigned"), .width(4)) comparator_2 (.a(bitselector_8_out), .b(4'b0000));  // open: gt, eq, lt
  Comparator #(.mode("unsigned"), .width(4)) comparator_3 (
    .a(bitselector_8_out), .b(4'b0001), .eq(comparator_3_eq));  // open: gt, lt
  Comparator #(.mode("unsigned"), .width(4)) comparator_4 (
    .a(bitselector_8_out), .b(4'b0010), .eq(comparator_4_eq));  // open: gt, lt
  Comparator #(.mode("unsigned"), .width(4)) comparator_5 (
    .a(bitselector_8_out), .b(4'b0011), .eq(comparator_5_eq));  // open: gt, lt
  Counter #(.max('h1), .trigger("falling"), .width(1)) counter_1 (
    .count(comparator_5_eq), .Q(counter_1_q), .clk(clock_2_out), .clr(not_1_out));  // open: load, D, carry, up
  not not_1 (not_1_out, comparator_5_eq);
  Clock clock_2 (.out(clock_2_out));
  BitSelector #(.width(16)) bitselector_12 (.in(bitselector_3_out), .out(bitselector_12_out), .sel(4'b0000));
  Comparator #(.mode("unsigned"), .width(4)) comparator_6 (
    .a(bitselector_8_out), .b(4'b0100), .eq(comparator_6_eq));  // open: gt, lt
  Multiplexer #(.select(2)) multiplexer_1 (
    .in0(comparator_7_eq), .in1(comparator_7_lt), .in2(fpcomparator_1_p8), .in3(fpcomparator_1_p9),
    .out(multiplexer_1_out), .sel(bitselector_9_out));
  Comparator #(.width(64)) comparator_7 (
    .a(fpcomparator_1_p6), .b({64{1'b0}}), .eq(comparator_7_eq), .lt(comparator_7_lt));  // open: gt
  // FPComparator #(.fpwidth(64)) fpcomparator_1: pin names not known; wires that end beside it: register_1_q, bitselector_1_out, bitselector_2_out, bitselector_3_out, bitselector_8_out, fpcomparator_1_p6, {64{1'b0}}, fpcomparator_1_p8, fpcomparator_1_p9
  and and_1 (and_1_out, bitselector_11_out, comparator_3_eq);
  or or_2 (or_2_out, comparator_4_eq, and_3_out, and_5_out);
  and and_2 (and_2_out, comparator_5_eq, comparator_8_lt);
  and and_3 (and_3_out, comparator_8_eq, not_2_out);
  not not_2 (not_2_out, bitselector_12_out);
  Comparator #(.mode("unsigned"), .width(1)) comparator_8 (
    .a(counter_1_q), .b(1'b1), .eq(comparator_8_eq), .lt(comparator_8_lt));  // open: gt
  and and_4 (and_4_out, comparator_8_eq, bitselector_12_out);
  and and_5 (and_5_out, comparator_6_eq, multiplexer_1_out);
  assign or_3_out = shifter_1_out | registry_1_regxout;  // OR_Gate or_3, 64 bits wide
  Shifter #(.width(64)) shifter_1 (.in(64'h1), .\dist (bitselector_10_out), .out(shifter_1_out));
  or or_4 (or_4_out, comparator_3_eq, or_2_out, comparator_8_eq, comparator_6_eq);
  Multiplexer #(.select(4), .width(64)) multiplexer_2 (
    .in0(ram_1_dout), .in1(ram_1_dout), .in2({{32{1'b0}}, bitselector_2_out, bitselector_3_out}),
    .in3(ram_1_dout), .in4(or_3_out), .out(multiplexer_2_out), .sel(bitselector_8_out));  // open: in5, in6, in7, in8, in9, in10, in11, in12, in13, in14, in15
  buf or_5 (or_5_out, comparator_8_eq);  // OR_Gate
  registry registry_1 (
    .value(multiplexer_2_out), .update(or_2_out), .regX(bitselector_5_out), .regY(bitselector_6_out),
    .regXout(registry_1_regxout), .regYout(fpcomparator_1_p6));
  not not_3 (not_3_out, or_5_out);
  BitSelector #(.group(16), .width(64)) bitselector_13 (.in(registry_1_regxout), .out(bitselector_13_out), .sel(2'b00));
  Register #(.width(64)) register_2 (
    .D(fpcomparator_1_p6), .en(and_2_out), .clk(clock_3_out), .Q(register_2_q));  // open: clr
  Clock clock_3 (.out(clock_3_out));
  Register #(.width(1)) register_3 (.D(and_2_out), .en(1'b1), .clk(clock_3_out), .Q(register_3_q));  // open: clr
  Counter #(.max('hffff), .width(16)) counter_2 (
    .load(and_1_out), .D(bitselector_13_out), .count(not_3_out), .Q(counter_2_q), .clk(clock_4_out));  // open: carry, up, clr
  Clock clock_4 (.out(clock_4_out));
  Multiplexer #(.width(16)) multiplexer_3 (
    .in0(counter_2_q), .in1(bitselector_14_out), .out(multiplexer_3_out), .sel(register_3_q));
  BitSelector #(.group(16), .width(64)) bitselector_14 (.in(register_2_q), .out(bitselector_14_out), .sel(2'b00));
  Multiplexer #(.select(4), .width(16)) multiplexer_4 (
    .in0(counter_2_q), .in1(counter_2_q), .in2(counter_2_q), .in3(multiplexer_3_out), .in4(counter_2_q),
    .out(multiplexer_4_out), .sel(bitselector_8_out));  // open: in5, in6, in7, in8, in9, in10, in11, in12, in13, in14, in15
  Clock clock_5 (.out(clock_5_out));
  Multiplexer #(.select(4)) multiplexer_5 (
    .in0(1'b0), .in1(1'b0), .in2(1'b0), .in3(and_4_out), .in4(1'b0), .out(multiplexer_5_out),
    .sel(bitselector_8_out));  // open: in5, in6, in7, in8, in9, in10, in11, in12, in13, in14, in15
  Multiplexer #(.select(4), .width(64)) multiplexer_6 (
    .in0({64{1'b0}}), .in1({64{1'b0}}), .in2({64{1'b0}}), .in3(registry_1_regxout), .in4({64{1'b0}}),
    .out(multiplexer_6_out), .sel(bitselector_8_out));  // open: in5, in6, in7, in8, in9, in10, in11, in12, in13, in14, in15
  RAM #(.addrWidth(16), .dataWidth(64), .enables("line"), .\type ("nonvolatile")) ram_1 (
    .addr(multiplexer_4_out), .we(multiplexer_5_out), .clk(clock_5_out), .din(multiplexer_6_out),
    .dout(ram_1_dout));
endmodule

module registry (
  input  [63:0] value,
  input  update,
  input  [5:0] regX,
  input  [5:0] regY,
  output [63:0] regXout,
  output [63:0] regYout
);

  wire clock_1_out, clock_2_out, clock_3_out, clock_4_out, clock_5_out, clock_6_out, clock_7_out,
       clock_8_out, clock_9_out, clock_10_out, clock_11_out, clock_12_out, clock_13_out, clock_14_out,
       clock_15_out, clock_16_out, clock_17_out, clock_18_out, clock_19_out, clock_20_out, clock_21_out,
       clock_22_out, clock_23_out, clock_24_out, clock_25_out, clock_26_out, clock_27_out, clock_28_out,
       clock_29_out, clock_30_out, clock_31_out, clock_32_out, clock_33_out, clock_34_out, clock_35_out,
       clock_36_out, clock_37_out, clock_38_out, clock_39_out, clock_40_out, clock_41_out, clock_42_out,
       clock_43_out, clock_44_out, clock_45_out, clock_46_out, clock_47_out, clock_48_out, clock_49_out,
       clock_50_out, clock_51_out, clock_52_out, clock_53_out, clock_54_out, clock_55_out, clock_56_out,
       clock_57_out, clock_58_out, clock_59_out, clock_60_out, clock_61_out, clock_62_out, clock_63_out,
       clock_64_out, u1, u2, u3, u4, u5, u6, u7, u8, u9, u10, u11, u12, u13, u14, u15, u16, u17, u18, u19,
       u20, u21, u22, u23, u24, u25, u26, u27, u28, u29, u30, u31, u32, u33, u34, u35, u36, u37, u38, u39,
       u40, u41, u42, u43, u44, u45, u46, u47, u48, u49, u50, u51, u52, u53, u54, u55, u56, u57, u58, u59,
       u60, u61, u62, u63, u64;
  wire [63:0] v1, v2, v3, v4, v5, v6, v7, v8, v9, v10, v11, v12, v13, v14, v15, v16, v17, v18, v19, v20, v21,
       v22, v23, v24, v25, v26, v27, v28, v29, v30, v31, v32, v33, v34, v35, v36, v37, v38, v39, v40, v41,
       v42, v43, v44, v45, v46, v47, v48, v49, v50, v51, v52, v53, v54, v55, v56, v57, v58, v59, v60, v61,
       v62, v63, v64;

  Demultiplexer #(.select(6)) demultiplexer_1 (
    .out0(u1), .out1(u2), .out2(u3), .out3(u4), .out4(u5), .out5(u6), .out6(u7), .out7(u8), .out8(u9),
    .out9(u10), .out10(u11), .out11(u12), .out12(u13), .out13(u14), .out14(u15), .out15(u16), .out16(u17),
    .out17(u18), .out18(u19), .out19(u20), .out20(u21), .out21(u22), .out22(u23), .out23(u24), .out24(u25),
    .out25(u26), .out26(u27), .out27(u28), .out28(u29), .out29(u30), .out30(u31), .out31(u32), .out32(u33),
    .out33(u34), .out34(u35), .out35(u36), .out36(u37), .out37(u38), .out38(u39), .out39(u40), .out40(u41),
    .out41(u42), .out42(u43), .out43(u44), .out44(u45), .out45(u46), .out46(u47), .out47(u48), .out48(u49),
    .out49(u50), .out50(u51), .out51(u52), .out52(u53), .out53(u54), .out54(u55), .out55(u56), .out56(u57),
    .out57(u58), .out58(u59), .out59(u60), .out60(u61), .out61(u62), .out62(u63), .out63(u64), .in(update),
    .sel(regX));
  Register #(.width(64)) register_1 (.D(value), .en(u1), .clk(clock_1_out), .Q(v1));  // open: clr
  Clock clock_1 (.out(clock_1_out));
  Register #(.width(64)) register_2 (.D(value), .en(u9), .clk(clock_2_out), .Q(v9));  // open: clr
  Clock clock_2 (.out(clock_2_out));
  Register #(.width(64)) register_3 (.D(value), .en(u17), .clk(clock_3_out), .Q(v17));  // open: clr
  Clock clock_3 (.out(clock_3_out));
  Register #(.width(64)) register_4 (.D(value), .en(u25), .clk(clock_4_out), .Q(v25));  // open: clr
  Clock clock_4 (.out(clock_4_out));
  Register #(.width(64)) register_5 (.D(value), .en(u33), .clk(clock_5_out), .Q(v33));  // open: clr
  Clock clock_5 (.out(clock_5_out));
  Register #(.width(64)) register_6 (.D(value), .en(u41), .clk(clock_6_out), .Q(v41));  // open: clr
  Clock clock_6 (.out(clock_6_out));
  Register #(.width(64)) register_7 (.D(value), .en(u49), .clk(clock_7_out), .Q(v49));  // open: clr
  Clock clock_7 (.out(clock_7_out));
  Register #(.width(64)) register_8 (.D(value), .en(u57), .clk(clock_8_out), .Q(v57));  // open: clr
  Clock clock_8 (.out(clock_8_out));
  Register #(.width(64)) register_9 (.D(value), .en(u2), .clk(clock_9_out), .Q(v2));  // open: clr
  Clock clock_9 (.out(clock_9_out));
  Register #(.width(64)) register_10 (.D(value), .en(u10), .clk(clock_10_out), .Q(v10));  // open: clr
  Clock clock_10 (.out(clock_10_out));
  Register #(.width(64)) register_11 (.D(value), .en(u18), .clk(clock_11_out), .Q(v18));  // open: clr
  Clock clock_11 (.out(clock_11_out));
  Register #(.width(64)) register_12 (.D(value), .en(u26), .clk(clock_12_out), .Q(v26));  // open: clr
  Clock clock_12 (.out(clock_12_out));
  Register #(.width(64)) register_13 (.D(value), .en(u34), .clk(clock_13_out), .Q(v34));  // open: clr
  Clock clock_13 (.out(clock_13_out));
  Register #(.width(64)) register_14 (.D(value), .en(u42), .clk(clock_14_out), .Q(v42));  // open: clr
  Clock clock_14 (.out(clock_14_out));
  Register #(.width(64)) register_15 (.D(value), .en(u50), .clk(clock_15_out), .Q(v50));  // open: clr
  Clock clock_15 (.out(clock_15_out));
  Register #(.width(64)) register_16 (.D(value), .en(u58), .clk(clock_16_out), .Q(v58));  // open: clr
  Clock clock_16 (.out(clock_16_out));
  Register #(.width(64)) register_17 (.D(value), .en(u3), .clk(clock_17_out), .Q(v3));  // open: clr
  Clock clock_17 (.out(clock_17_out));
  Register #(.width(64)) register_18 (.D(value), .en(u11), .clk(clock_18_out), .Q(v11));  // open: clr
  Clock clock_18 (.out(clock_18_out));
  Register #(.width(64)) register_19 (.D(value), .en(u19), .clk(clock_19_out), .Q(v19));  // open: clr
  Clock clock_19 (.out(clock_19_out));
  Register #(.width(64)) register_20 (.D(value), .en(u27), .clk(clock_20_out), .Q(v27));  // open: clr
  Clock clock_20 (.out(clock_20_out));
  Register #(.width(64)) register_21 (.D(value), .en(u35), .clk(clock_21_out), .Q(v35));  // open: clr
  Clock clock_21 (.out(clock_21_out));
  Register #(.width(64)) register_22 (.D(value), .en(u43), .clk(clock_22_out), .Q(v43));  // open: clr
  Clock clock_22 (.out(clock_22_out));
  Register #(.width(64)) register_23 (.D(value), .en(u51), .clk(clock_23_out), .Q(v51));  // open: clr
  Clock clock_23 (.out(clock_23_out));
  Register #(.width(64)) register_24 (.D(value), .en(u59), .clk(clock_24_out), .Q(v59));  // open: clr
  Clock clock_24 (.out(clock_24_out));
  Register #(.width(64)) register_25 (.D(value), .en(u4), .clk(clock_25_out), .Q(v4));  // open: clr
  Clock clock_25 (.out(clock_25_out));
  Register #(.width(64)) register_26 (.D(value), .en(u12), .clk(clock_26_out), .Q(v12));  // open: clr
  Clock clock_26 (.out(clock_26_out));
  Register #(.width(64)) register_27 (.D(value), .en(u20), .clk(clock_27_out), .Q(v20));  // open: clr
  Clock clock_27 (.out(clock_27_out));
  Register #(.width(64)) register_28 (.D(value), .en(u28), .clk(clock_28_out), .Q(v28));  // open: clr
  Clock clock_28 (.out(clock_28_out));
  Register #(.width(64)) register_29 (.D(value), .en(u36), .clk(clock_29_out), .Q(v36));  // open: clr
  Clock clock_29 (.out(clock_29_out));
  Register #(.width(64)) register_30 (.D(value), .en(u44), .clk(clock_30_out), .Q(v44));  // open: clr
  Clock clock_30 (.out(clock_30_out));
  Register #(.width(64)) register_31 (.D(value), .en(u52), .clk(clock_31_out), .Q(v52));  // open: clr
  Clock clock_31 (.out(clock_31_out));
  Register #(.width(64)) register_32 (.D(value), .en(u60), .clk(clock_32_out), .Q(v60));  // open: clr
  Clock clock_32 (.out(clock_32_out));
  Register #(.width(64)) register_33 (.D(value), .en(u5), .clk(clock_33_out), .Q(v5));  // open: clr
  Clock clock_33 (.out(clock_33_out));
  Register #(.width(64)) register_34 (.D(value), .en(u13), .clk(clock_34_out), .Q(v13));  // open: clr
  Clock clock_34 (.out(clock_34_out));
  Register #(.width(64)) register_35 (.D(value), .en(u21), .clk(clock_35_out), .Q(v21));  // open: clr
  Clock clock_35 (.out(clock_35_out));
  Register #(.width(64)) register_36 (.D(value), .en(u29), .clk(clock_36_out), .Q(v29));  // open: clr
  Clock clock_36 (.out(clock_36_out));
  Register #(.width(64)) register_37 (.D(value), .en(u37), .clk(clock_37_out), .Q(v37));  // open: clr
  Clock clock_37 (.out(clock_37_out));
  Register #(.width(64)) register_38 (.D(value), .en(u45), .clk(clock_38_out), .Q(v45));  // open: clr
  Clock clock_38 (.out(clock_38_out));
  Register #(.width(64)) register_39 (.D(value), .en(u53), .clk(clock_39_out), .Q(v53));  // open: clr
  Clock clock_39 (.out(clock_39_out));
  Register #(.width(64)) register_40 (.D(value), .en(u61), .clk(clock_40_out), .Q(v61));  // open: clr
  Clock clock_40 (.out(clock_40_out));
  Register #(.width(64)) register_41 (.D(value), .en(u6), .clk(clock_41_out), .Q(v6));  // open: clr
  Clock clock_41 (.out(clock_41_out));
  Register #(.width(64)) register_42 (.D(value), .en(u14), .clk(clock_42_out), .Q(v14));  // open: clr
  Clock clock_42 (.out(clock_42_out));
  Register #(.width(64)) register_43 (.D(value), .en(u22), .clk(clock_43_out), .Q(v22));  // open: clr
  Clock clock_43 (.out(clock_43_out));
  Register #(.width(64)) register_44 (.D(value), .en(u30), .clk(clock_44_out), .Q(v30));  // open: clr
  Clock clock_44 (.out(clock_44_out));
  Register #(.width(64)) register_45 (.D(value), .en(u38), .clk(clock_45_out), .Q(v38));  // open: clr
  Clock clock_45 (.out(clock_45_out));
  Register #(.width(64)) register_46 (.D(value), .en(u46), .clk(clock_46_out), .Q(v46));  // open: clr
  Clock clock_46 (.out(clock_46_out));
  Register #(.width(64)) register_47 (.D(value), .en(u54), .clk(clock_47_out), .Q(v54));  // open: clr
  Clock clock_47 (.out(clock_47_out));
  Register #(.width(64)) register_48 (.D(value), .en(u62), .clk(clock_48_out), .Q(v62));  // open: clr
  Clock clock_48 (.out(clock_48_out));
  Register #(.width(64)) register_49 (.D(value), .en(u7), .clk(clock_49_out), .Q(v7));  // open: clr
  Clock clock_49 (.out(clock_49_out));
  Register #(.width(64)) register_50 (.D(value), .en(u15), .clk(clock_50_out), .Q(v15));  // open: clr
  Clock clock_50 (.out(clock_50_out));
  Register #(.width(64)) register_51 (.D(value), .en(u23), .clk(clock_51_out), .Q(v23));  // open: clr
  Clock clock_51 (.out(clock_51_out));
  Register #(.width(64)) register_52 (.D(value), .en(u31), .clk(clock_52_out), .Q(v31));  // open: clr
  Clock clock_52 (.out(clock_52_out));
  Register #(.width(64)) register_53 (.D(value), .en(u39), .clk(clock_53_out), .Q(v39));  // open: clr
  Clock clock_53 (.out(clock_53_out));
  Register #(.width(64)) register_54 (.D(value), .en(u47), .clk(clock_54_out), .Q(v47));  // open: clr
  Clock clock_54 (.out(clock_54_out));
  Register #(.width(64)) register_55 (.D(value), .en(u55), .clk(clock_55_out), .Q(v55));  // open: clr
  Clock clock_55 (.out(clock_55_out));
  Register #(.width(64)) register_56 (.D(value), .en(u63), .clk(clock_56_out), .Q(v63));  // open: clr
  Clock clock_56 (.out(clock_56_out));
  Register #(.width(64)) register_57 (.D(value), .en(u8), .clk(clock_57_out), .Q(v8));  // open: clr
  Clock clock_57 (.out(clock_57_out));
  Register #(.width(64)) register_58 (.D(value), .en(u16), .clk(clock_58_out), .Q(v16));  // open: clr
  Clock clock_58 (.out(clock_58_out));
  Register #(.width(64)) register_59 (.D(value), .en(u24), .clk(clock_59_out), .Q(v24));  // open: clr
  Clock clock_59 (.out(clock_59_out));
  Register #(.width(64)) register_60 (.D(value), .en(u32), .clk(clock_60_out), .Q(v32));  // open: clr
  Clock clock_60 (.out(clock_60_out));
  Register #(.width(64)) register_61 (.D(value), .en(u40), .clk(clock_61_out), .Q(v40));  // open: clr
  Clock clock_61 (.out(clock_61_out));
  Register #(.width(64)) register_62 (.D(value), .en(u48), .clk(clock_62_out), .Q(v48));  // open: clr
  Clock clock_62 (.out(clock_62_out));
  Register #(.width(64)) register_63 (.D(value), .en(u56), .clk(clock_63_out), .Q(v56));  // open: clr
  Clock clock_63 (.out(clock_63_out));
  Register #(.width(64)) register_64 (.D(value), .en(u64), .clk(clock_64_out), .Q(v64));  // open: clr
  Clock clock_64 (.out(clock_64_out));
  Multiplexer #(.select(6), .width(64)) multiplexer_1 (
    .in0(v1), .in1(v2), .in2(v3), .in3(v4), .in4(v5), .in5(v6), .in6(v7), .in7(v8), .in8(v9), .in9(v10),
    .in10(v11), .in11(v12), .in12(v13), .in13(v14), .in14(v15), .in15(v16), .in16(v17), .in17(v18),
    .in18(v19), .in19(v20), .in20(v21), .in21(v22), .in22(v23), .in23(v24), .in24(v25), .in25(v26),
    .in26(v27), .in27(v28), .in28(v29), .in29(v30), .in30(v31), .in31(v32), .in32(v33), .in33(v34),
    .in34(v35), .in35(v36), .in36(v37), .in37(v38), .in38(v39), .in39(v40), .in40(v41), .in41(v42),
    .in42(v43), .in43(v44), .in44(v45), .in45(v46), .in46(v47), .in47(v48), .in48(v49), .in49(v50),
    .in50(v51), .in51(v52), .in52(v53), .in53(v54), .in54(v55), .in55(v56), .in56(v57), .in57(v58),
    .in58(v59), .in59(v60), .in60(v61), .in61(v62), .in62(v63), .in63(v64), .out(regXout), .sel(regX));
  Multiplexer #(.select(6), .width(64)) multiplexer_2 (
    .in0(v1), .in1(v2), .in2(v3), .in3(v4), .in4(v5), .in5(v6), .in6(v7), .in7(v8), .in8(v9), .in9(v10),
    .in10(v11), .in11(v12), .in12(v13), .in13(v14), .in14(v15), .in15(v16), .in16(v17), .in17(v18),
    .in18(v19), .in19(v20), .in20(v21), .in21(v22), .in22(v23), .in23(v24), .in24(v25), .in25(v26),
    .in26(v27), .in27(v28), .in28(v29), .in29(v30), .in30(v31), .in31(v32), .in32(v33), .in33(v34),
    .in34(v35), .in35(v36), .in36(v37), .in37(v38), .in38(v39), .in39(v40), .in40(v41), .in41(v42),
    .in42(v43), .in43(v44), .in44(v45), .in45(v46), .in46(v47), .in47(v48), .in48(v49), .in49(v50),
    .in50(v51), .in51(v52), .in52(v53), .in53(v54), .in54(v55), .in55(v56), .in56(v57), .in57(v58),
    .in58(v59), .in59(v60), .in60(v61), .in61(v62), .in62(v63), .in63(v64), .out(regYout), .sel(regY));
endmodule
